# Fritzing sketch MotorController (saved by Fritzing 0.9.9b)
circuit board: 7cm x 5.5cm

parts:
  TB6612FNG = Motor Driver 1A Dual TB6612FNG
  J1 = Screw terminal - 2 pins [package=THT]
  J2 = Screw terminal - 2 pins [package=THT]
  Part1 = Arduino Pro Mini v13
  J6 = JST-03JQ-BT [part_number=JST-JQ-BT package=THT]
  J7 = JST-03JQ-BT [part_number=JST-JQ-BT package=THT]
  J8 = female pin header, 2 pins [form="♀ (female)"]
  J9 = female pin header, 2 pins [form="♀ (female)"]
  J10 = female pin header, 2 pins [form="♀ (female)"]
  J11 = female pin header, 2 pins [form="♀ (female)"]
  J12 = female pin header, 2 pins [form="♀ (female)"]
  J13 = female pin header, 2 pins [form="♀ (female)"]
  J14 = female pin header, 2 pins [form="♀ (female)"]
  J15 = female pin header, 2 pins [form="♀ (female)"]
  J16 = female pin header, 2 pins [form="♀ (female)"]
  J17 = female pin header, 2 pins [form="♀ (female)"]
  J18 = female pin header, 2 pins [form="♀ (female)"]

nets:
  GND: TB6612FNG.GND, Part1.GND, J6.pin1, J7.pin1, J8.pin2, J9.pin2, J10.pin2, J11.pin2, J12.pin2, J13.pin2, J14.pin2, J15.pin2, J16.pin2, J18.pin1
  N1: TB6612FNG.B01, J2.pin2
  N2: TB6612FNG.B02, J2.pin1
  N3: TB6612FNG.A02, J1.pin2
  N4: TB6612FNG.A01, J1.pin1
  VCC: TB6612FNG.VCC, Part1.VCC, J6.pin2, J7.pin2, J9.pin1, J11.pin1, J12.pin1, J13.pin1, J18.pin2
  N5: TB6612FNG.VM, J10.pin1
  N6: TB6612FNG.PWMA, Part1.D5_PWM
  N7: TB6612FNG.AIN2, Part1.D6_PWM
  N8: TB6612FNG.AIN1, Part1.D7
  N9: TB6612FNG.STBY, Part1.D8
  N10: TB6612FNG.BIN1, Part1.D9_PWM
  N11: TB6612FNG.BIN2, Part1.D10_PWM/SS
  N12: TB6612FNG.PWMB, Part1.D11_PWM/MOSI
  N13: Part1.A3, J17.pin1
  N14: Part1.A2, J17.pin2
  N15: Part1.D3_PWM, J7.pin3
  N16: Part1.D2, J6.pin3
  N17: J8.pin1, J14.pin1, J15.pin1, J16.pin1

notes:
  GND
  5V
  VMOT
  3V3
  VIN
  VOUT
  MOTOR A
  MOTOR B
  SDA
  SCL
  I2C
