# Fritzing sketch robot-platform (saved by Fritzing 0.9.3b)

parts:
  U1 = TB6612FNG [package=so016]
  Part1 = Arduino Nano (Rev3.0)
  Right_Motor = DC Motor
  Left_Motor = DC Motor
  9v_Battery_Pack_(6AA) = DC Power [voltage=9]
  S1 = Toggle Switch [package=THT]
  Part2 = Bluetooth HC-05 Macho

nets:
  VCC: U1.VCC, Part1.5V, Part2.VCC
  N1: U1.AO1, Left_Motor.pin_2
  N2: U1.AO2, Left_Motor.pin_1
  N3: U1.BO2, Right_Motor.pin_2
  N4: U1.BO1, Right_Motor.pin_1
  N5: U1.VMOT, Part1.VIN, S1.COM
  GND: U1.GND#7, Part1.GND, 9v_Battery_Pack_(6AA).V-, Part2.GND
  N6: U1.AIN1, Part1.D11/MOSI
  N7: U1.AIN2, Part1.D10
  N8: U1.STBY, Part1.D9
  N9: U1.BIN1, Part1.D8
  N10: U1.BIN2, Part1.D7
  N11: U1.PWMB, Part1.D6
  N12: U1.GND#15, Part1.D5
  N13: Part1.D1/TX, Part2.TXD
  N14: Part1.D0/RX, Part2.RXD
  N15: 9v_Battery_Pack_(6AA).V+, S1.L2

notes:
  Robot Platform

custom parts:
  TB6612FNG: TB6612FNG Dual Motor Driver Carrier
