# Fritzing sketch robot-platform-v2 (saved by Fritzing 0.9.9b)
circuit board: 9.98cm x 6.44989cm
stripboards: 2

parts:
  U1 = TB6612FNG [package=so016]
  Part1 = Arduino Nano (Rev3.0)
  Right_Motor = DC Motor
  Left_Motor = DC Motor
  MCU1 = Raspberry Pi Zero
  6V_Motor_Power = Screw terminal - 2 pins [package=THT]
  5V_Regulated_Power = Screw terminal - 2 pins [package=THT]
  Part4 = I2C level shifter bidirectional
  Enc1 = shaft encoder
  Enc2 = shaft encoder

nets:
  GND: U1.GND#0, Part1.GND, MCU1.pin_6, MCU1.pin_34, MCU1.pin_39, 5V_Regulated_Power.pin2, Part4.GND, Enc1.GND, Enc2.GND
  5V: U1.VCC, Part1.5V, MCU1.pin_2, MCU1.pin_4, 5V_Regulated_Power.pin1, Part4.HV, Enc1.VCC, Enc2.VCC
  N1: U1.AO1, Left_Motor.pin_2
  N2: U1.AO2, Left_Motor.pin_1
  N3: U1.BO2, Right_Motor.pin_2
  N4: U1.BO1, Right_Motor.pin_1
  N5: U1.VMOT, 6V_Motor_Power.pin2
  N6: U1.GND#7, 6V_Motor_Power.pin1
  N7: U1.AIN1, Part1.D11/MOSI
  N8: U1.AIN2, Part1.D10
  N9: U1.STBY, Part1.D9
  N10: U1.BIN1, Part1.D8
  N11: U1.BIN2, Part1.D7
  N12: U1.PWMB, Part1.D6
  N13: U1.GND#15, Part1.D5
  N14: Part1.D2, Enc2.OUT
  N15: Part1.D3, Enc1.OUT
  N16: Part1.A5, Part4.HV2
  N17: Part1.A4, Part4.HV1
  N18: MCU1.pin_1, Part4.LV
  N19: MCU1.pin_3, Part4.LV1
  N20: MCU1.pin_5, Part4.LV2

notes:
  5V Regulated Power
  Motor Power Supply
  Robot Platform
  I2CBus
  5V
  3.3v

custom parts:
  TB6612FNG: TB6612FNG Dual Motor Driver Carrier
